// Logisim project ALU design.circ as structural Verilog: 2 circuits, main circuit main
module main (
  input  CS0,
  input  CS1,
  input  CS2,
  input  A1,
  input  B1,
  input  A2,
  input  B2,
  input  A3,
  input  B3,
  input  A4,
  input  B4,
  output out_12,
  output out_13,
  output out_14,
  output V,
  output SF,
  output ZF,
  output CF
);

  wire and_1_out, and_2_out, and_3_out, and_4_out, and_5_out, and_6_out, and_7_out, and_8_out, and_9_out,
       and_10_out, and_11_out, and_12_out, and_13_out, and_14_out, and_15_out, and_16_out, and_17_out,
       and_18_out, and_19_out, n1bit_full_adder_1_out_5, n1bit_full_adder_2_out_5, n1bit_full_adder_3_out_5,
       n1bit_full_adder_4_out_5, not_1_out, not_2_out, not_3_out, not_4_out, not_5_out, not_6_out, not_7_out,
       not_8_out, or_1_out, or_2_out, or_3_out, or_4_out, or_5_out, or_6_out, or_7_out, or_8_out, or_9_out,
       or_10_out, or_11_out, or_12_out, or_13_out, or_14_out, or_15_out, xor_1_out;

  and and_1 (and_1_out, CS1, CS2);
  not not_1 (not_1_out, CS2);
  and and_2 (and_2_out, not_1_out, CS1);
  and and_3 (and_3_out, B1, and_1_out);
  not not_2 (not_2_out, B1);
  and and_4 (and_4_out, B2, and_1_out);
  not not_3 (not_3_out, B2);
  and and_5 (and_5_out, B3, and_1_out);
  not not_4 (not_4_out, B3);
  and and_6 (and_6_out, B4, and_1_out);
  not not_5 (not_5_out, B4);
  and and_7 (and_7_out, and_2_out, not_2_out);
  and and_8 (and_8_out, and_2_out, not_3_out);
  and and_9 (and_9_out, and_2_out, not_4_out);
  and and_10 (and_10_out, and_2_out, not_5_out);
  not not_6 (not_6_out, CS1);
  not not_7 (not_7_out, CS2);
  and and_11 (and_11_out, not_7_out, not_6_out);
  or or_1 (or_1_out, and_3_out, and_7_out);
  or or_2 (or_2_out, and_4_out, and_8_out);
  or or_3 (or_3_out, and_5_out, and_9_out);
  or or_4 (or_4_out, and_6_out, and_10_out);
  not not_8 (not_8_out, CS1);
  and and_12 (and_12_out, and_11_out, B1);
  and and_13 (and_13_out, and_11_out, B2);
  and and_14 (and_14_out, and_11_out, B3);
  and and_15 (and_15_out, and_11_out, B4);
  or or_5 (or_5_out, A1, and_7_out);
  or or_6 (or_6_out, or_1_out, and_12_out);
  or or_7 (or_7_out, A2, and_8_out);
  or or_8 (or_8_out, or_2_out, and_13_out);
  or or_9 (or_9_out, A3, and_9_out);
  or or_10 (or_10_out, or_3_out, and_14_out);
  or or_11 (or_11_out, A4, and_10_out);
  or or_12 (or_12_out, or_4_out, and_15_out);
  and and_16 (and_16_out, CS0, not_8_out);
  and and_17 (and_17_out, not_8_out, n1bit_full_adder_1_out_5);
  and and_18 (and_18_out, not_8_out, n1bit_full_adder_2_out_5);
  and and_19 (and_19_out, not_8_out, n1bit_full_adder_3_out_5);
  _1bit_full_adder u_1bit_full_adder_1 (
    .in_1(or_5_out), .in_2(or_6_out), .in_3(and_16_out), .out_4(out_12), .out_5(n1bit_full_adder_1_out_5));
  _1bit_full_adder u_1bit_full_adder_2 (
    .in_1(or_7_out), .in_2(or_8_out), .in_3(and_17_out), .out_4(out_13), .out_5(n1bit_full_adder_2_out_5));
  or or_13 (or_13_out, out_12, out_13);
  or or_14 (or_14_out, or_13_out, out_14);
  _1bit_full_adder u_1bit_full_adder_3 (
    .in_1(or_9_out), .in_2(or_10_out), .in_3(and_18_out), .out_4(out_14), .out_5(n1bit_full_adder_3_out_5));
  _1bit_full_adder u_1bit_full_adder_4 (
    .in_1(or_11_out), .in_2(or_12_out), .in_3(and_19_out), .out_4(SF), .out_5(n1bit_full_adder_4_out_5));
  xor xor_1 (xor_1_out, n1bit_full_adder_3_out_5, n1bit_full_adder_4_out_5);
  not not_9 (ZF, or_15_out);
  or or_15 (or_15_out, or_14_out, SF);
  and and_20 (CF, n1bit_full_adder_4_out_5, not_8_out);
  and and_21 (V, not_8_out, xor_1_out);

  // Notes on the sheet:
  //   CS2CS1
  //   CS2'CS1
  //   CS2'CS1'
  //   X1
  //   Y1
  //   X2
  //   Y2
  //   X3
  //   Y3
  //   X4
  //   Y4
  //   CS1'CS0
  //   C1
  //   C2
  //   C3
  //   Cout
  //   S1
  //   S2
  //   S3
  //   S4
endmodule

module _1bit_full_adder (
  input  in_1,
  input  in_2,
  input  in_3,
  output out_4,
  output out_5
);

  wire and_1_out, and_2_out, xor_1_out;

  xor xor_1 (xor_1_out, in_1, in_2);
  and and_1 (and_1_out, in_2, in_1);
  xor xor_2 (out_4, xor_1_out, in_3);
  and and_2 (and_2_out, xor_1_out, in_3);
  or or_1 (out_5, and_2_out, and_1_out);
endmodule
