// Logisim project MIPS.circ as structural Verilog
module main (
  input  [2:0] in_1,
  input  Clear,
  output [7:0] out_3
);

  wire CLK_out, mips_alu_8_bit_by_tushar_1_p4;
  wire [7:0] mips_alu_8_bit_by_tushar_1_p5, register_1_q, register_file_1_read_data1,
       register_file_1_read_data2;
  wire [19:0] rom_1_data;

  Register #(.trigger("falling")) register_1 (.D(out_3), .Q(register_1_q), .clk(CLK_out), .clr(Clear));  // open: en
  Clock CLK (.out(CLK_out));
  Adder adder_1 (.a(register_1_q), .b(8'h1), .out(out_3), .cin(1'b0));  // open: cout
  ROM #(.dataWidth(20)) rom_1 (.addr(register_1_q), .data(rom_1_data));  // open: sel
  Register_file register_file_1 (
    .Read_Register_1(rom_1_data[15:12]), .Read_Register_2(rom_1_data[11:8]),
    .Write_Data(mips_alu_8_bit_by_tushar_1_p5), .Write_Register(rom_1_data[7:4]),
    .Read_Data1(register_file_1_read_data1), .Read_Data2(register_file_1_read_data2));  // open: RegWrite, CLK, MemOp
  // MIPS_ALU_8_bit_by_Tushar mips_alu_8_bit_by_tushar_1: pin names not known; wires that end beside it: register_file_1_read_data1, register_file_1_read_data2, in_1, mips_alu_8_bit_by_tushar_1_p4, mips_alu_8_bit_by_tushar_1_p5, mips_alu_8_bit_by_tushar_1_p4
endmodule

module _8_bit_ALU (
  input  [7:0] Operand_A,
  input  [7:0] Operand_B,
  input  [2:0] Operation,
  output Zero,
  output [7:0] Result,
  output Overflow
);

  // MIPS_ALU_8_bit_by_Tushar mips_alu_8_bit_by_tushar_1: pin names not known; wires that end beside it: Operand_A, Operand_B, Operation, Zero, Result, Overflow
endmodule

module Register_file (
  input  MemOp,
  input  [3:0] Read_Register_1,
  input  [3:0] Read_Register_2,
  input  [7:0] Write_Data,
  input  RegWrite,
  input  CLK,
  input  [3:0] Write_Register,
  output [7:0] Read_Data1,
  output [7:0] Read_Data2
);

  wire and_1_out, demultiplexer_1_out0, demultiplexer_1_out1, demultiplexer_1_out2, demultiplexer_1_out3,
       demultiplexer_1_out4, demultiplexer_1_out5, demultiplexer_1_out6;
  wire [7:0] t0_q, t1_q, zero_q;

  and and_1 (and_1_out, RegWrite, CLK);
  Demultiplexer #(.select(3), .enable("false")) demultiplexer_1 (
    .out0(demultiplexer_1_out0), .out1(demultiplexer_1_out1), .out2(demultiplexer_1_out2),
    .out3(demultiplexer_1_out3), .out4(demultiplexer_1_out4), .out5(demultiplexer_1_out5),
    .out6(demultiplexer_1_out6), .in(and_1_out), .sel(Write_Register[2:0]));  // open: out7
  Register zero (.D({8{1'b0}}), .Q(zero_q), .clk(demultiplexer_1_out0));  // open: en, clr
  Register t0 (.D(Write_Data), .Q(t0_q), .clk(demultiplexer_1_out1));  // open: en, clr
  Register t1 (.D(Write_Data), .Q(t1_q), .clk(demultiplexer_1_out2));  // open: en, clr
  Register t2 (.D(Write_Data), .Q(t1_q), .clk(demultiplexer_1_out3));  // open: en, clr
  Register t3 (.D(Write_Data), .Q(t1_q), .clk(demultiplexer_1_out4));  // open: en, clr
  Register t4 (.D(Write_Data), .Q(t1_q), .clk(demultiplexer_1_out5));  // open: en, clr
  Register sp (.D(Write_Data), .Q(t1_q), .clk(demultiplexer_1_out6));  // open: en, clr
  Multiplexer #(.select(3), .width(8), .enable("false")) multiplexer_1 (
    .in0(zero_q), .in1(t0_q), .in2(t1_q), .in3(t1_q), .in4(t1_q), .in5(t1_q), .in6(t1_q), .in7({8{1'b0}}),
    .out(Read_Data1), .sel(Read_Register_1[2:0]));
  Multiplexer #(.select(3), .width(8), .enable("false")) multiplexer_2 (
    .in0(zero_q), .in1(t0_q), .in2(t1_q), .in3(t1_q), .in4(t1_q), .in5(t1_q), .in6(t1_q), .in7({8{1'b0}}),
    .out(Read_Data2), .sel(Read_Register_2[2:0]));
endmodule

module Instruction_Memory (
  input  [7:0] Instruction_Address
);
endmodule

module Data_Memory (
  input  MemRead,
  input  [7:0] Address,
  input  MemWrite,
  input  [7:0] WriteData,
  output [7:0] ReadDara
);

  wire and_1_out, Clk_out;

  Clock Clk (.out(Clk_out));
  and and_1 (and_1_out, Clk_out, MemWrite);
endmodule
