// Logisim project Pipelining.circ as structural Verilog: 10 circuits, main circuit main
module main (
  input  Wrt,
  input  [7:0] ExWD,
  input  [3:0] ExWA,
  input  Clear,
  output [7:0] out_5,
  output AEW
);

  wire and_2_out, CLK_2_out, CLK_out, control_unit_1_regdst, not_1_out, not_2_out, not_3_out, not_4_out,
       not_5_out, not_6_out, not_7_out, not_8_out, or_1_out;
  wire [1:0] control_unit_1_memtoreg, control_unit_1_memwrite, ex_mem_1_memcontrol_2, ex_mem_1_wbcontrol_2,
       forwardingunit_1_forwarda, forwardingunit_1_forwardb, id_ex_1_memcontrol_2, id_ex_1_wbcontrol_2,
       mem_wb_1_wbcontrol_2;
  wire [3:0] ex_mem_1_writeaddress_2, id_ex_1_id_ex_rs, id_ex_1_id_ex_rt, id_ex_1_writeaddress_2,
       mem_wb_1_writeaddress_2, multiplexer_1_out, multiplexer_3_out;
  wire [5:0] control_unit_1_aluop, id_ex_1_excontrol_2;
  wire [7:0] bit_extender_1_out, data_memory_1_readdata, ex_mem_1_aluresult_2, ex_mem_1_writedata_2,
       id_ex_1_immediate_2, id_ex_1_regdata1_2, id_ex_1_regdata2_2, id_ex_1_target_2,
       if_id_1_instruction_2_2, mem_wb_1_aluresult_2, mem_wb_1_memdata_2, mips_alu_8_bit_by_tushar_2_p5,
       multiplexer_2_out, multiplexer_4_out, multiplexer_5_out, multiplexer_6_out, multiplexer_7_out,
       multiplexer_8_out, register_1_q, register_file_1_readdata1, register_file_1_readdata2;
  wire [19:0] rom_1_data;
  wire [19:8] if_id_1_instruction_2;

  Clock CLK (.out(CLK_out));
  Register #(.trigger("falling")) register_1 (.D(out_5), .Q(register_1_q), .clk(CLK_out), .clr(Clear));  // open: en
  // MIPS_ALU_8_bit_by_Tushar mips_alu_8_bit_by_tushar_1: pin names not known; wires that end beside it: register_1_q, 8'h1, 3'b000, out_5, out_5
  ROM #(.dataWidth(20)) rom_1 (.addr(register_1_q), .data(rom_1_data));  // open: sel
  IF_ID if_id_1 (
    .Clear(Clear), .CLK(not_1_out), .Instruction(rom_1_data),
    .Instruction_2({if_id_1_instruction_2, if_id_1_instruction_2_2}));
  not not_1 (not_1_out, CLK_out);
  assign bit_extender_1_out = {{4{1'b0}}, if_id_1_instruction_2_2[3:0]};  // Bit_Extender bit_extender_1
  not not_2 (not_2_out, mem_wb_1_wbcontrol_2[1]);
  and and_1 (AEW, not_2_out, Wrt);
  or or_1 (or_1_out, mem_wb_1_wbcontrol_2[1], AEW);
  Multiplexer #(.width(4), .enable("false")) multiplexer_1 (
    .in0(if_id_1_instruction_2[11:8]), .in1(if_id_1_instruction_2_2[7:4]), .out(multiplexer_1_out),
    .sel(control_unit_1_regdst));
  Multiplexer #(.width(8), .enable("false")) multiplexer_2 (
    .in0(multiplexer_8_out), .in1(ExWD), .out(multiplexer_2_out), .sel(AEW));
  Control_Unit control_unit_1 (
    .Opcode(if_id_1_instruction_2[19:16]), .RegWrite(control_unit_1_memtoreg[1]),
    .ALUSrcA(control_unit_1_aluop[3]), .MemWrite(control_unit_1_memwrite[0]),
    .ALUOp(control_unit_1_aluop[2:0]), .MemtoReg(control_unit_1_memtoreg[0]),
    .MemRead(control_unit_1_memwrite[1]), .RegDst(control_unit_1_regdst), .ALUSrcB(control_unit_1_aluop[5:4]));  // open: BranchEqual, Jump, BranchNotEqual
  Register_file register_file_1 (
    .ReadRegister1(if_id_1_instruction_2[15:12]), .ReadRegister2(if_id_1_instruction_2[11:8]),
    .ReadData1(register_file_1_readdata1), .ReadData2(register_file_1_readdata2),
    .WriteData(multiplexer_2_out), .WriteRegister(multiplexer_3_out), .RegWrite(or_1_out), .CLK(and_2_out),
    .Reset(Clear));
  and and_2 (and_2_out, not_3_out, not_4_out);
  Multiplexer #(.width(4), .enable("false")) multiplexer_3 (
    .in0(mem_wb_1_writeaddress_2), .in1(ExWA), .out(multiplexer_3_out), .sel(AEW));
  not not_3 (not_3_out, CLK_2_out);
  Clock CLK_2 (.out(CLK_2_out));
  not not_4 (not_4_out, CLK_out);
  ID_EX id_ex_1 (
    .WBControl(control_unit_1_memtoreg), .MemControl(control_unit_1_memwrite),
    .ExControl(control_unit_1_aluop), .RegData1(register_file_1_readdata1),
    .RegData2(register_file_1_readdata2), .Immediate(bit_extender_1_out), .Target(if_id_1_instruction_2_2),
    .WriteAddress(multiplexer_1_out), .CLK(not_5_out), .Clear(Clear), .WBControl_2(id_ex_1_wbcontrol_2),
    .MemControl_2(id_ex_1_memcontrol_2), .ExControl_2(id_ex_1_excontrol_2), .RegData1_2(id_ex_1_regdata1_2),
    .RegData2_2(id_ex_1_regdata2_2), .Immediate_2(id_ex_1_immediate_2), .Target_2(id_ex_1_target_2),
    .WriteAddress_2(id_ex_1_writeaddress_2), .IF_ID_Rs(if_id_1_instruction_2[15:12]),
    .ID_EX_Rs(id_ex_1_id_ex_rs), .IF_ID_Rt(if_id_1_instruction_2[11:8]), .ID_EX_Rt(id_ex_1_id_ex_rt));
  not not_5 (not_5_out, CLK_out);
  Multiplexer #(.select(2), .width(8), .enable("false")) multiplexer_4 (
    .in0(id_ex_1_regdata2_2), .in1(id_ex_1_target_2), .in2(id_ex_1_regdata1_2), .in3({8{1'b0}}),
    .out(multiplexer_4_out), .sel(id_ex_1_excontrol_2[5:4]));
  Multiplexer #(.width(8), .enable("false")) multiplexer_5 (
    .in0(id_ex_1_regdata1_2), .in1(id_ex_1_immediate_2), .out(multiplexer_5_out), .sel(id_ex_1_excontrol_2[3]));
  ForwardingUnit forwardingunit_1 (
    .MEM_WB_RegWrite(mem_wb_1_wbcontrol_2[1]), .MEM_WB_Rd(mem_wb_1_writeaddress_2),
    .EX_MEM_RegWrite(ex_mem_1_wbcontrol_2[1]), .EX_MEM_Rd(ex_mem_1_writeaddress_2),
    .ID_EX_Rs(id_ex_1_id_ex_rs), .ID_EX_Rt(id_ex_1_id_ex_rt), .ForwardA(forwardingunit_1_forwarda),
    .ForwardB(forwardingunit_1_forwardb));
  Multiplexer #(.select(2), .width(8), .enable("false")) multiplexer_6 (
    .in0(multiplexer_5_out), .in1(multiplexer_8_out), .in2(ex_mem_1_aluresult_2), .out(multiplexer_6_out),
    .sel(forwardingunit_1_forwarda));  // open: in3
  Multiplexer #(.select(2), .width(8), .enable("false")) multiplexer_7 (
    .in0(multiplexer_4_out), .in1(multiplexer_8_out), .in2(ex_mem_1_aluresult_2), .out(multiplexer_7_out),
    .sel(forwardingunit_1_forwardb));  // open: in3
  // MIPS_ALU_8_bit_by_Tushar mips_alu_8_bit_by_tushar_2: pin names not known; wires that end beside it: multiplexer_4_out, multiplexer_6_out, multiplexer_7_out, id_ex_1_excontrol_2[2:0], mips_alu_8_bit_by_tushar_2_p5
  EX_MEM ex_mem_1 (
    .WBControl(id_ex_1_wbcontrol_2), .MemControl(id_ex_1_memcontrol_2),
    .ALUResult(mips_alu_8_bit_by_tushar_2_p5), .WriteData(id_ex_1_regdata2_2),
    .WriteAddress(id_ex_1_writeaddress_2), .CLK(not_6_out), .Clear(Clear),
    .WBControl_2(ex_mem_1_wbcontrol_2), .MemControl_2(ex_mem_1_memcontrol_2),
    .ALUResult_2(ex_mem_1_aluresult_2), .WriteData_2(ex_mem_1_writedata_2),
    .WriteAddress_2(ex_mem_1_writeaddress_2));
  not not_6 (not_6_out, CLK_out);
  Data_Memory data_memory_1 (
    .Address(ex_mem_1_aluresult_2), .WriteData(ex_mem_1_writedata_2), .MemRead(ex_mem_1_memcontrol_2[1]),
    .MemWrite(ex_mem_1_memcontrol_2[0]), .ReadData(data_memory_1_readdata), .CLK(not_7_out), .Reset(Clear));
  not not_7 (not_7_out, CLK_out);
  MEM_WB mem_wb_1 (
    .WBControl(ex_mem_1_wbcontrol_2), .MemData(data_memory_1_readdata), .ALUResult(ex_mem_1_aluresult_2),
    .WriteAddress(ex_mem_1_writeaddress_2), .CLK(not_8_out), .Clear(Clear),
    .WBControl_2(mem_wb_1_wbcontrol_2), .MemData_2(mem_wb_1_memdata_2), .ALUResult_2(mem_wb_1_aluresult_2),
    .WriteAddress_2(mem_wb_1_writeaddress_2));
  not not_8 (not_8_out, CLK_out);
  Multiplexer #(.width(8), .enable("false")) multiplexer_8 (
    .in0(mem_wb_1_aluresult_2), .in1(mem_wb_1_memdata_2), .out(multiplexer_8_out),
    .sel(mem_wb_1_wbcontrol_2[0]));

  // Notes on the sheet:
  //   PC
  //   Instruction Memory
  //   contents of rom_1 (hex, n*v repeats v):
  //   e3420 a2350 c2450 e5450
endmodule

module _8_bit_ALU (
  input  [7:0] Operand_A,
  input  [7:0] Operand_B,
  input  [2:0] Operation,
  output Zero,
  output [7:0] Result,
  output Overflow
);

  // MIPS_ALU_8_bit_by_Tushar mips_alu_8_bit_by_tushar_1: pin names not known; wires that end beside it: Operand_A, Operand_B, Operation, Zero, Result, Overflow
endmodule

module Register_file (
  input  [3:0] ReadRegister1,
  input  [3:0] ReadRegister2,
  input  [7:0] WriteData,
  input  RegWrite,
  input  [3:0] WriteRegister,
  input  CLK,
  input  Reset,
  output [7:0] ReadData1,
  output [7:0] ReadData2
);

  wire demultiplexer_1_out0, demultiplexer_1_out1, demultiplexer_1_out2, demultiplexer_1_out3,
       demultiplexer_1_out4, demultiplexer_1_out5, demultiplexer_1_out6, demultiplexer_1_out7;
  wire [7:0] multiplexer_3_out, sp_q, t0_q, t1_q, t2_q, t3_q, t4_q, t5_q, zero_q;

  Demultiplexer #(.select(3), .enable("false")) demultiplexer_1 (
    .out0(demultiplexer_1_out0), .out1(demultiplexer_1_out1), .out2(demultiplexer_1_out2),
    .out3(demultiplexer_1_out3), .out4(demultiplexer_1_out4), .out5(demultiplexer_1_out5),
    .out6(demultiplexer_1_out6), .out7(demultiplexer_1_out7), .in(RegWrite), .sel(WriteRegister[2:0]));
  Register #(.trigger("falling")) zero (.D({8{1'b0}}), .en(demultiplexer_1_out0), .Q(zero_q), .clk(CLK), .clr(Reset));
  Register #(.trigger("falling")) t0 (.D(WriteData), .en(demultiplexer_1_out1), .Q(t0_q), .clk(CLK), .clr(Reset));
  Register #(.trigger("falling")) t2 (.D(WriteData), .en(demultiplexer_1_out3), .Q(t2_q), .clk(CLK), .clr(Reset));
  Register #(.trigger("falling")) t1 (.D(WriteData), .en(demultiplexer_1_out2), .Q(t1_q), .clk(CLK), .clr(Reset));
  Register #(.trigger("falling")) t3 (.D(WriteData), .en(demultiplexer_1_out4), .Q(t3_q), .clk(CLK), .clr(Reset));
  Register #(.trigger("falling")) t4 (.D(WriteData), .en(demultiplexer_1_out5), .Q(t4_q), .clk(CLK), .clr(Reset));
  Register #(.trigger("falling")) t5 (.D(WriteData), .en(demultiplexer_1_out6), .Q(t5_q), .clk(CLK), .clr(Reset));
  Multiplexer #(.select(3), .width(8), .enable("false")) multiplexer_1 (
    .in0(zero_q), .in1(t0_q), .in2(t1_q), .in3(t2_q), .in4(t3_q), .in5(t4_q), .in6(t5_q), .in7(sp_q),
    .out(ReadData1), .sel(ReadRegister1[2:0]));
  Multiplexer #(.select(3), .width(8), .enable("false")) multiplexer_2 (
    .in0(zero_q), .in1(t0_q), .in2(t1_q), .in3(t2_q), .in4(t3_q), .in5(t4_q), .in6(t5_q), .in7(sp_q),
    .out(ReadData2), .sel(ReadRegister2[2:0]));
  Register #(.trigger("falling")) sp (
    .D(multiplexer_3_out), .en(demultiplexer_1_out7), .Q(sp_q), .clk(CLK));  // open: clr
  Multiplexer #(.width(8), .enable("false")) multiplexer_3 (
    .in0(WriteData), .in1({8{1'b1}}), .out(multiplexer_3_out), .sel(Reset));
endmodule

module Control_Unit (
  input  [3:0] Opcode,
  output RegWrite,
  output ALUSrcA,
  output MemWrite,
  output [2:0] ALUOp,
  output MemtoReg,
  output MemRead,
  output BranchEqual,
  output Jump,
  output RegDst,
  output BranchNotEqual,
  output [1:0] ALUSrcB
);

  wire [15:14] rom_1_data;

  ROM #(.addrWidth(4), .dataWidth(16)) rom_1 (
    .addr(Opcode),
    .data({rom_1_data, ALUSrcB, BranchNotEqual, RegDst, Jump, BranchEqual, MemRead, MemtoReg, ALUOp, MemWrite, ALUSrcA, RegWrite}));  // open: sel

  // Notes on the sheet:
  //   contents of rom_1 (hex, n*v repeats v):
  //   242b 419 10c1 1019 200 1009 2433 108 421 1004 409 1011 411 1001 401 808
endmodule

module Data_Memory (
  input  [7:0] Address,
  input  [7:0] WriteData,
  input  MemRead,
  input  MemWrite,
  input  CLK,
  input  Reset,
  output [7:0] ReadData
);

  wire and_1_out;

  and and_1 (and_1_out, MemWrite, CLK);
  RAM #(.bus("separate")) ram_1 (
    .addr(Address), .din(WriteData), .data(ReadData), .str(MemWrite), .clk(and_1_out), .ld(MemRead),
    .clr(Reset));  // open: sel
endmodule

module IF_ID (
  input  Clear,
  input  CLK,
  input  [19:0] Instruction,
  output [19:0] Instruction_2
);

  Register #(.width(20), .trigger("falling")) register_1 (
    .D(Instruction), .Q(Instruction_2), .clk(CLK), .clr(Clear));  // open: en
endmodule

module ID_EX (
  input  [1:0] WBControl,
  input  [1:0] MemControl,
  input  [5:0] ExControl,
  input  [7:0] RegData1,
  input  [7:0] RegData2,
  input  [7:0] Immediate,
  input  [7:0] Target,
  input  [3:0] IF_ID_Rs,
  input  [3:0] IF_ID_Rt,
  input  [3:0] WriteAddress,
  input  CLK,
  input  Clear,
  output [1:0] WBControl_2,
  output [1:0] MemControl_2,
  output [5:0] ExControl_2,
  output [7:0] RegData1_2,
  output [7:0] RegData2_2,
  output [7:0] Immediate_2,
  output [7:0] Target_2,
  output [3:0] ID_EX_Rs,
  output [3:0] ID_EX_Rt,
  output [3:0] WriteAddress_2
);

  Register #(.width(2), .trigger("falling")) register_1 (
    .D(WBControl), .Q(WBControl_2), .clk(CLK), .clr(Clear));  // open: en
  Register #(.width(2), .trigger("falling")) register_2 (
    .D(MemControl), .Q(MemControl_2), .clk(CLK), .clr(Clear));  // open: en
  Register #(.width(6), .trigger("falling")) register_3 (
    .D(ExControl), .Q(ExControl_2), .clk(CLK), .clr(Clear));  // open: en
  Register #(.trigger("falling")) register_4 (.D(RegData1), .Q(RegData1_2), .clk(CLK), .clr(Clear));  // open: en
  Register #(.trigger("falling")) register_5 (.D(RegData2), .Q(RegData2_2), .clk(CLK), .clr(Clear));  // open: en
  Register #(.trigger("falling")) register_6 (.D(Immediate), .Q(Immediate_2), .clk(CLK), .clr(Clear));  // open: en
  Register #(.trigger("falling")) register_7 (.D(Target), .Q(Target_2), .clk(CLK), .clr(Clear));  // open: en
  Register #(.width(4), .trigger("falling")) register_8 (
    .D(IF_ID_Rs), .Q(ID_EX_Rs), .clk(CLK), .clr(Clear));  // open: en
  Register #(.width(4), .trigger("falling")) register_9 (
    .D(IF_ID_Rt), .Q(ID_EX_Rt), .clk(CLK), .clr(Clear));  // open: en
  Register #(.width(4), .trigger("falling")) register_10 (
    .D(WriteAddress), .Q(WriteAddress_2), .clk(CLK), .clr(Clear));  // open: en
endmodule

module EX_MEM (
  input  [1:0] WBControl,
  input  [1:0] MemControl,
  input  [7:0] ALUResult,
  input  [7:0] WriteData,
  input  [3:0] WriteAddress,
  input  CLK,
  input  Clear,
  output [1:0] WBControl_2,
  output [1:0] MemControl_2,
  output [7:0] ALUResult_2,
  output [7:0] WriteData_2,
  output [3:0] WriteAddress_2
);

  Register #(.width(2), .trigger("falling")) register_1 (
    .D(WBControl), .Q(WBControl_2), .clk(CLK), .clr(Clear));  // open: en
  Register #(.width(2), .trigger("falling")) register_2 (
    .D(MemControl), .Q(MemControl_2), .clk(CLK), .clr(Clear));  // open: en
  Register #(.trigger("falling")) register_3 (.D(ALUResult), .Q(ALUResult_2), .clk(CLK), .clr(Clear));  // open: en
  Register #(.trigger("falling")) register_4 (.D(WriteData), .Q(WriteData_2), .clk(CLK), .clr(Clear));  // open: en
  Register #(.width(4), .trigger("falling")) register_5 (
    .D(WriteAddress), .Q(WriteAddress_2), .clk(CLK), .clr(Clear));  // open: en
endmodule

module MEM_WB (
  input  [1:0] WBControl,
  input  [7:0] MemData,
  input  [7:0] ALUResult,
  input  [3:0] WriteAddress,
  input  CLK,
  input  Clear,
  output [1:0] WBControl_2,
  output [7:0] MemData_2,
  output [7:0] ALUResult_2,
  output [3:0] WriteAddress_2
);

  Register #(.width(2), .trigger("falling")) register_1 (
    .D(WBControl), .Q(WBControl_2), .clk(CLK), .clr(Clear));  // open: en
  Register #(.trigger("falling")) register_2 (.D(MemData), .Q(MemData_2), .clk(CLK), .clr(Clear));  // open: en
  Register #(.trigger("falling")) register_3 (.D(ALUResult), .Q(ALUResult_2), .clk(CLK), .clr(Clear));  // open: en
  Register #(.width(4), .trigger("falling")) register_4 (
    .D(WriteAddress), .Q(WriteAddress_2), .clk(CLK), .clr(Clear));  // open: en
endmodule

module ForwardingUnit (
  input  EX_MEM_RegWrite,
  input  [3:0] EX_MEM_Rd,
  input  [3:0] ID_EX_Rs,
  input  [3:0] ID_EX_Rt,
  input  MEM_WB_RegWrite,
  input  [3:0] MEM_WB_Rd,
  output [1:0] ForwardA,
  output [1:0] ForwardB
);

  wire and_1_out, and_2_out, comparator_1_eq, comparator_2_eq, comparator_3_eq, comparator_4_eq,
       comparator_5_eq, comparator_6_eq, not_1_out, not_2_out, not_3_out, not_4_out, or_1_out, or_2_out;
  wire [0:0] and_5_out, and_6_out;
  wire [1:0] multiplexer_1_out, multiplexer_2_out;
  wire [1:1] and_3_out, and_4_out;

  Comparator #(.width(4), .mode("unsigned")) comparator_1 (
    .a(EX_MEM_Rd), .b(4'b0000), .eq(comparator_1_eq));  // open: gt, lt
  Comparator #(.width(4), .mode("unsigned")) comparator_2 (
    .a(EX_MEM_Rd), .b(ID_EX_Rs), .eq(comparator_2_eq));  // open: gt, lt
  Comparator #(.width(4), .mode("unsigned")) comparator_3 (
    .a(MEM_WB_Rd), .b(4'b0000), .eq(comparator_3_eq));  // open: gt, lt
  not not_1 (not_1_out, comparator_1_eq);
  Comparator #(.width(4), .mode("unsigned")) comparator_4 (
    .a(EX_MEM_Rd), .b(ID_EX_Rt), .eq(comparator_4_eq));  // open: gt, lt
  not not_2 (not_2_out, and_4_out[1]);
  Comparator #(.width(4), .mode("unsigned")) comparator_5 (
    .a(MEM_WB_Rd), .b(ID_EX_Rs), .eq(comparator_5_eq));  // open: gt, lt
  Comparator #(.width(4), .mode("unsigned")) comparator_6 (
    .a(MEM_WB_Rd), .b(ID_EX_Rt), .eq(comparator_6_eq));  // open: gt, lt
  and and_1 (and_1_out, MEM_WB_RegWrite, not_3_out);
  not not_3 (not_3_out, comparator_3_eq);
  and and_2 (and_2_out, EX_MEM_RegWrite, not_1_out);
  not not_4 (not_4_out, and_3_out[1]);
  and and_3 (and_3_out[1], and_2_out, comparator_2_eq);
  and and_4 (and_4_out[1], and_2_out, comparator_4_eq);
  and and_5 (and_5_out[0], not_4_out, comparator_5_eq, and_1_out);
  and and_6 (and_6_out[0], not_2_out, comparator_6_eq, and_1_out);
  or or_1 (or_1_out, and_3_out[1], and_5_out[0]);
  or or_2 (or_2_out, and_4_out[1], and_6_out[0]);
  Multiplexer #(.width(2), .enable("false")) multiplexer_1 (
    .in0({1'b0, and_5_out[0]}), .in1({and_3_out[1], 1'b0}), .out(multiplexer_1_out), .sel(and_3_out[1]));
  Multiplexer #(.width(2), .enable("false")) multiplexer_2 (
    .in0({1'b0, and_6_out[0]}), .in1({and_4_out[1], 1'b0}), .out(multiplexer_2_out), .sel(and_4_out[1]));
  Multiplexer #(.width(2), .enable("false")) multiplexer_3 (
    .in0(2'b00), .in1(multiplexer_1_out), .out(ForwardA), .sel(or_1_out));
  Multiplexer #(.width(2), .enable("false")) multiplexer_4 (
    .in0(2'b00), .in1(multiplexer_2_out), .out(ForwardB), .sel(or_2_out));
endmodule
